// Logisim project codificator.circ as structural Verilog: 1 circuit, main circuit main
module main (
  input  I3,
  input  I2,
  input  I1,
  input  I0,
  output O1,
  output O0
);

  wire not_1_out, not_2_out, not_3_out, not_4_out;

  not not_1 (not_1_out, I3);
  not not_2 (not_2_out, I1);
  not not_3 (not_3_out, I3);
  not not_4 (not_4_out, I2);
  and and_1 (O1, not_1_out, not_2_out);
  and and_2 (O0, not_3_out, not_4_out);
endmodule
