// Logisim project demultiplexer.circ as structural Verilog: 1 circuit, main circuit main
module main (
  input  I,
  input  Sel,
  output Out_1,
  output Out_0
);

  wire not_1_out;

  not not_1 (not_1_out, Sel);
  and and_1 (Out_1, I, Sel);
  and and_2 (Out_0, I, not_1_out);
endmodule
