// Logisim project fullAdder.circ as structural Verilog: 1 circuit, main circuit main
module main (
  input  X,
  input  Y,
  input  Cin,
  output R,
  output Cout
);

  wire and_1_out, and_2_out, and_3_out;

  ExactlyOne xor_1 (.out(R), .in0(X), .in1(Y), .in2(Cin));
  and and_1 (and_1_out, X, Y);
  and and_2 (and_2_out, X, Cin);
  and and_3 (and_3_out, Y, Cin);
  or or_1 (Cout, and_1_out, and_2_out, and_3_out);
endmodule
