// Logisim project parityGenerator3b.circ as structural Verilog: 1 circuit, main circuit main
module main (
  input  E_2,
  input  E_1,
  input  E_0,
  output Output
);

  wire xor_1_out;

  xor xor_1 (xor_1_out, E_2, E_1);
  xnor xnor_1 (Output, xor_1_out, E_0);
endmodule
