// Logisim project latchJK.circ as structural Verilog: 1 circuit, main circuit main
module main (
  input  K,
  input  E,
  input  J,
  output Q,
  output Q_prime
);

  wire nand_1_out, nand_2_out;

  nand nand_1 (nand_1_out, Q, K, E);
  nand nand_2 (nand_2_out, E, J, Q_prime);
  nor nor_1 (Q, nand_1_out, Q_prime);
  nor nor_2 (Q_prime, Q, nand_2_out);
endmodule
