// Logisim project comparator.circ as structural Verilog: 1 circuit, main circuit main
module main (
  input  X,
  input  Y,
  output out_3,
  output out_4,
  output out_5
);

  wire not_1_out, not_2_out;

  not not_1 (not_1_out, Y);
  not not_2 (not_2_out, X);
  and and_1 (out_3, X, not_1_out);
  and and_2 (out_4, not_2_out, Y);
  xnor xnor_1 (out_5, X, Y);
endmodule
