// Logisim project decodificator.circ as structural Verilog: 1 circuit, main circuit main
module main (
  input  D1,
  input  D0,
  output S3,
  output S2,
  output S1,
  output S0
);

  wire and_3_out, and_4_out, and_5_out, and_6_out, not_1_out, not_2_out, not_3_out, not_4_out, not_5_out,
       not_6_out, not_7_out, not_8_out, not_9_out;

  not not_1 (not_1_out, D1);
  not not_2 (not_2_out, D1);
  not not_3 (not_3_out, D0);
  not not_4 (not_4_out, D1);
  not not_5 (not_5_out, D0);
  not not_6 (not_6_out, D0);
  not not_7 (not_7_out, D1);
  not not_8 (not_8_out, D0);
  not not_9 (not_9_out, D1);
  and and_1 (S3, D0, not_1_out);
  and and_2 (S2, not_2_out, not_3_out);
  and and_3 (and_3_out, not_4_out, not_5_out);
  and and_4 (and_4_out, D1, not_6_out);
  and and_5 (and_5_out, not_7_out, not_8_out);
  and and_6 (and_6_out, not_9_out, D0);
  or or_1 (S1, and_3_out, and_4_out);
  or or_2 (S0, and_5_out, and_6_out);
endmodule
