// Logisim project fullSubtractor.circ as structural Verilog: 1 circuit, main circuit main
module main (
  input  M,
  input  S,
  input  B,
  output DIF,
  output V
);

  wire and_1_out, and_2_out, and_3_out, not_1_out, not_2_out;

  ExactlyOne xor_1 (.out(DIF), .in0(M), .in1(S), .in2(B));
  not not_1 (not_1_out, M);
  not not_2 (not_2_out, M);
  and and_1 (and_1_out, not_1_out, S);
  and and_2 (and_2_out, not_2_out, B);
  and and_3 (and_3_out, S, B);
  nor nor_1 (V, and_1_out, and_2_out, and_3_out);
endmodule
