// Logisim project halfAdder.circ as structural Verilog: 1 circuit, main circuit main
module main (
  input  A,
  input  B,
  output R,
  output V
);

  xor xor_1 (R, A, B);
  and and_1 (V, A, B);
endmodule
