// Logisim project halfSubtractor.circ as structural Verilog: 1 circuit, main circuit main
module main (
  input  X,
  input  Y,
  output R,
  output Cout
);

  wire not_1_out;

  not not_1 (not_1_out, X);
  xor xor_1 (R, X, Y);
  and and_1 (Cout, not_1_out, Y);
endmodule
