// Logisim project latchRS.circ as structural Verilog: 1 circuit, main circuit main
module main (
  input  Set,
  input  Reset,
  output Q,
  output Q_prime
);

  wire not_1_out, not_2_out;

  not not_1 (not_1_out, Set);
  not not_2 (not_2_out, Reset);
  nand nand_1 (Q, not_1_out, Q_prime);
  nand nand_2 (Q_prime, not_2_out, Q);
endmodule
