// Logisim project multiplexer.circ as structural Verilog: 1 circuit, main circuit main
module main (
  input  Entrada_1,
  input  Entrada_2,
  input  Seletor,
  output \Saída 
);

  wire and_1_out, and_2_out, not_1_out;

  not not_1 (not_1_out, Seletor);
  and and_1 (and_1_out, Entrada_1, not_1_out);
  and and_2 (and_2_out, Entrada_2, Seletor);
  or or_1 (\Saída , and_1_out, and_2_out);
endmodule
